// Logisim project alu.circ as structural Verilog: 1 circuit, main circuit alu
module alu (
  input  [31:0] A,
  input  [31:0] B,
  input  [3:0] ALUSel,
  output [31:0] Result
);

  wire [0:0] sir_14, slt13;
  wire [1:0] comparator_3_eq;
  wire [6:0] sir_15;
  wire [31:0] add_3, adder_2_out, and0, bit_extender_1_out, bit_extender_2_out, div9, divider_2_out,
       divider_4_out, divu8, mulh7, mult5, multhu6, multiplier_2_out, multiplier_3_out, negator_1_out,
       negator_2_out, negator_3_out, negator_4_out, or1, output_01, output_10, output_11, remu10, sra12,
       srl11, sub_4, undriven, undriven_2, xor2;

  Subtractor #(.width(32)) subtractor_1 (.a(A), .b(B), .out(sub_4));  // open: bin, bout
  Multiplier #(.width(32)) multiplier_1 (.a(undriven), .b(undriven_2), .out(mult5), .cout(multhu6));  // open: cin
  Adder #(.width(32)) adder_1 (.a(A), .b(B), .out(add_3));  // open: cin, cout
  assign and0 = A & B;  // AND_Gate and_1, 32 bits wide
  assign or1 = A | B;  // OR_Gate or_1, 32 bits wide
  assign xor2 = A ^ B;  // XOR_Gate xor_1, 32 bits wide
  Shifter #(.width(32), .shift("lr")) shifter_1 (.in(A), .\dist (B[4:0]), .out(srl11));
  Shifter #(.width(32), .shift("ar")) shifter_2 (.in(A), .\dist (B[4:0]), .out(sra12));
  Comparator #(.width(32)) comparator_1 (.a(A), .b(B), .lt(slt13[0]));  // open: gt, eq
  BitAdder #(.width(32)) bitadder_1 (.in0(A), .in1(B), .out(sir_15));
  Divider #(.width(32)) divider_1 (.a(A), .b(B), .out(divu8), .rem(remu10));  // open: upper
  Comparator #(.width(32)) comparator_2 (
    .a(A),
    .b({B[0], B[1], B[2], B[3], B[4], B[5], B[6], B[7], B[8], B[9], B[10], B[11], B[12], B[13], B[14], B[15], B[16], B[17], B[18], B[19], B[20], B[21], B[22], B[23], B[24], B[25], B[26], B[27], B[28], B[29], B[30], B[31]}),
    .eq(sir_14[0]));  // open: gt, lt
  Multiplexer #(.select(4), .width(32), .enable("false")) multiplexer_1 (
    .in0(and0), .in1(or1), .in2(xor2), .in3(add_3), .in4(sub_4), .in5(mult5), .in6(multhu6), .in7(mulh7),
    .in8(divu8), .in9(div9), .in10(remu10), .in11(srl11), .in12(sra12), .in13({{31{1'b0}}, slt13[0]}),
    .in14({{31{1'b0}}, sir_14[0]}), .in15({{25{1'b0}}, sir_15}), .out(Result), .sel(ALUSel));
  assign bit_extender_1_out = {{31{A[31]}}, A[31]};  // Bit_Extender bit_extender_1
  assign bit_extender_2_out = {{31{B[31]}}, B[31]};  // Bit_Extender bit_extender_2
  Negator #(.width(32)) negator_1 (.in(B), .out(negator_1_out));
  Negator #(.width(32)) negator_2 (.in(B), .out(negator_2_out));
  Negator #(.width(32)) negator_3 (.in(A), .out(negator_3_out));
  Multiplier #(.width(32)) multiplier_2 (.a(B), .b(bit_extender_1_out), .out(multiplier_2_out));  // open: cin, cout
  Multiplier #(.width(32)) multiplier_3 (.a(bit_extender_2_out), .b(A), .out(multiplier_3_out));  // open: cin, cout
  Comparator #(.width(1), .mode("unsigned")) comparator_3 (
    .a(1'b1), .b(A[31]), .eq(comparator_3_eq[0]));  // open: gt, lt
  Comparator #(.width(1), .mode("unsigned")) comparator_4 (
    .a(B[31]), .b(1'b1), .eq(comparator_3_eq[1]));  // open: gt, lt
  Negator #(.width(32)) negator_4 (.in(A), .out(negator_4_out));
  Divider #(.width(32)) divider_2 (.a(A), .b(negator_1_out), .out(divider_2_out));  // open: upper, rem
  Divider #(.width(32)) divider_3 (.a(negator_3_out), .b(negator_2_out), .out(output_11));  // open: upper, rem
  Adder #(.width(32)) adder_2 (.a(multiplier_2_out), .b(multiplier_3_out), .out(adder_2_out));  // open: cin, cout
  Divider #(.width(32)) divider_4 (.a(negator_4_out), .b(B), .out(divider_4_out));  // open: upper, rem
  Negator #(.width(32)) negator_5 (.in(divider_2_out), .out(output_10));
  Adder #(.width(32)) adder_3 (.a(adder_2_out), .b(multhu6), .out(mulh7));  // open: cin, cout
  Multiplexer #(.select(2), .width(32), .enable("false")) multiplexer_2 (
    .in0(divu8), .in1(output_01), .in2(output_10), .in3(output_11), .out(div9), .sel(comparator_3_eq));
  Negator #(.width(32)) negator_6 (.in(divider_4_out), .out(output_01));

  // Notes on the sheet:
  //   INPUTS to your circuit
  //   DON'T CHANGE THE LOCATIONS OF THE INPUTS AND OUTPUTS!
  //   OUTPUT from your circuit
endmodule
