// Logisim project regfile.circ as structural Verilog: 1 circuit, main circuit main
module main (
  input  [4:0] Read_Register_1_rs1,
  input  [4:0] Read_Register_2_rs2,
  input  [4:0] Write_Register_rd,
  input  [31:0] Write_Data,
  input  Write_Enable,
  input  Clock,
  output [31:0] ra,
  output [31:0] sp,
  output [31:0] t0,
  output [31:0] t1,
  output [31:0] t2,
  output [31:0] s0,
  output [31:0] s1,
  output [31:0] a0,
  output [31:0] Read_Data_1,
  output [31:0] Read_Data_2
);

  wire a0_W, ra_W, s0_W, s1_W, sp_W, t0_W, t1_W, t2_W;

  Demultiplexer #(.select(5), .enable("false")) demultiplexer_1 (
    .out1(ra_W), .out2(sp_W), .out5(t0_W), .out6(t1_W), .out7(t2_W), .out8(s0_W), .out9(s1_W), .out10(a0_W),
    .in(Write_Enable), .sel(Write_Register_rd));  // open: out0, out3, out4, out11, out12, out13, out14, out15, out16, out17, out18, out19, out20, out21, out22, out23, out24, out25, out26, out27, out28, out29, out30, out31
  Register #(.width(32)) register_1 (.D(Write_Data), .en(ra_W), .clk(Clock), .Q(ra));  // open: clr
  Register #(.width(32)) register_2 (.D(Write_Data), .en(sp_W), .clk(Clock), .Q(sp));  // open: clr
  Register #(.width(32)) register_3 (.D(Write_Data), .en(t0_W), .clk(Clock), .Q(t0));  // open: clr
  Register #(.width(32)) register_4 (.D(Write_Data), .en(t1_W), .clk(Clock), .Q(t1));  // open: clr
  Register #(.width(32)) register_5 (.D(Write_Data), .en(t2_W), .clk(Clock), .Q(t2));  // open: clr
  Register #(.width(32)) register_6 (.D(Write_Data), .en(s0_W), .clk(Clock), .Q(s0));  // open: clr
  Register #(.width(32)) register_7 (.D(Write_Data), .en(s1_W), .clk(Clock), .Q(s1));  // open: clr
  Register #(.width(32)) register_8 (.D(Write_Data), .en(a0_W), .clk(Clock), .Q(a0));  // open: clr
  Multiplexer #(.select(5), .width(32), .enable("false")) multiplexer_1 (
    .in0({32{1'b0}}), .in1(ra), .in2(sp), .in5(t0), .in6(t1), .in7(t2), .in8(s0), .in9(s1), .in10(a0),
    .out(Read_Data_1), .sel(Read_Register_1_rs1));  // open: in3, in4, in11, in12, in13, in14, in15, in16, in17, in18, in19, in20, in21, in22, in23, in24, in25, in26, in27, in28, in29, in30, in31
  Multiplexer #(.select(5), .width(32), .enable("false")) multiplexer_2 (
    .in0({32{1'b0}}), .in1(ra), .in2(sp), .in5(t0), .in6(t1), .in7(t2), .in8(s0), .in9(s1), .in10(a0),
    .out(Read_Data_2), .sel(Read_Register_2_rs2));  // open: in3, in4, in11, in12, in13, in14, in15, in16, in17, in18, in19, in20, in21, in22, in23, in24, in25, in26, in27, in28, in29, in30, in31

  // Other names for the same wires on the sheet: clk = Clock; read_data1[31:0] = Read_Data_1;
  //   read_data2[31:0] = Read_Data_2; read_reg1[4:0] = Read_Register_1_rs1; read_reg2[4:0] = Read_Register_2_rs2;
  //   write_en = Write_Enable; write_reg[4:0] = Write_Register_rd

  // Notes on the sheet:
  //   INPUTS to your circuit
  //   DON'T CHANGE THE LOCATIONS OF THE INPUTS AND OUTPUTS!
  //   These are DEBUG/TEST outputs from your circuit.
  //   OUTPUTS from your circuit
endmodule
