// Logisim project alu.circ as structural Verilog: 1 circuit, main circuit alu
module alu (
  input  [31:0] A,
  input  [31:0] B,
  input  [3:0] ALUSel,
  output [31:0] Result
);

  wire [0:0] slt13;
  wire [1:0] comparator_2_eq;
  wire [31:0] add_3, adder_2_out, and0, bit_extender_1_out, bit_extender_2_out, div9, divider_2_out,
       divider_4_out, divu8, mulh7, mult5, multhu6, multiplier_2_out, multiplier_3_out, negator_1_out,
       negator_2_out, negator_3_out, negator_4_out, or1, output_01, output_10, output_11, remu10, sll11,
       srl12, sub_4, xor2;

  Multiplexer #(.select(4), .width(32), .enable("false")) multiplexer_1 (
    .in0(add_3), .in1(mult5), .in2(sub_4), .in3(sll11), .in4(mulh7), .in5(multhu6), .in6(xor2), .in7(div9),
    .in8(divu8), .in9(srl12), .in10(or1), .in11(remu10), .in12(and0), .in13({{31{1'b0}}, slt13[0]}),
    .out(Result), .sel(ALUSel));  // open: in14, in15
  Subtractor #(.width(32)) subtractor_1 (.a(A), .b(B), .out(sub_4));  // open: bin, bout
  Comparator #(.width(32)) comparator_1 (.a(A), .b(B), .lt(slt13[0]));  // open: gt, eq
  Multiplier #(.width(32)) multiplier_1 (.a(A), .b(B), .out(mult5), .cout(multhu6));  // open: cin
  Adder #(.width(32)) adder_1 (.a(A), .b(B), .out(add_3));  // open: cin, cout
  assign and0 = A & B;  // AND_Gate and_1, 32 bits wide
  assign or1 = A | B;  // OR_Gate or_1, 32 bits wide
  assign xor2 = A ^ B;  // XOR_Gate xor_1, 32 bits wide
  Shifter #(.width(32)) shifter_1 (.in(A), .\dist (B[4:0]), .out(sll11));
  Shifter #(.width(32), .shift("lr")) shifter_2 (.in(A), .\dist (B[4:0]), .out(srl12));
  Divider #(.width(32)) divider_1 (.a(A), .b(B), .out(divu8), .rem(remu10));  // open: upper
  assign bit_extender_1_out = {{31{A[31]}}, A[31]};  // Bit_Extender bit_extender_1
  assign bit_extender_2_out = {{31{B[31]}}, B[31]};  // Bit_Extender bit_extender_2
  Negator #(.width(32)) negator_1 (.in(B), .out(negator_1_out));
  Negator #(.width(32)) negator_2 (.in(B), .out(negator_2_out));
  Negator #(.width(32)) negator_3 (.in(A), .out(negator_3_out));
  Multiplier #(.width(32)) multiplier_2 (.a(B), .b(bit_extender_1_out), .out(multiplier_2_out));  // open: cin, cout
  Multiplier #(.width(32)) multiplier_3 (.a(bit_extender_2_out), .b(A), .out(multiplier_3_out));  // open: cin, cout
  Comparator #(.width(1), .mode("unsigned")) comparator_2 (
    .a(1'b1), .b(A[31]), .eq(comparator_2_eq[0]));  // open: gt, lt
  Comparator #(.width(1), .mode("unsigned")) comparator_3 (
    .a(B[31]), .b(1'b1), .eq(comparator_2_eq[1]));  // open: gt, lt
  Negator #(.width(32)) negator_4 (.in(A), .out(negator_4_out));
  Divider #(.width(32)) divider_2 (.a(A), .b(negator_1_out), .out(divider_2_out));  // open: upper, rem
  Divider #(.width(32)) divider_3 (.a(negator_3_out), .b(negator_2_out), .out(output_11));  // open: upper, rem
  Adder #(.width(32)) adder_2 (.a(multiplier_2_out), .b(multiplier_3_out), .out(adder_2_out));  // open: cin, cout
  Divider #(.width(32)) divider_4 (.a(negator_4_out), .b(B), .out(divider_4_out));  // open: upper, rem
  Negator #(.width(32)) negator_5 (.in(divider_2_out), .out(output_10));
  Adder #(.width(32)) adder_3 (.a(adder_2_out), .b(multhu6), .out(mulh7));  // open: cin, cout
  Multiplexer #(.select(2), .width(32), .enable("false")) multiplexer_2 (
    .in0(divu8), .in1(output_01), .in2(output_10), .in3(output_11), .out(div9), .sel(comparator_2_eq));
  Negator #(.width(32)) negator_6 (.in(divider_4_out), .out(output_01));

  // Notes on the sheet:
  //   INPUTS to your circuit
  //   DON'T CHANGE THE LOCATIONS OF THE INPUTS AND OUTPUTS!
  //   OUTPUT from your circuit
endmodule
