// Logisim project cpu.circ as structural Verilog: 6 circuits, main circuit main
module main (
  input  [31:0] INSTRUCTION,
  input  CLOCK,
  output [31:0] FETCH_ADDRESS,
  output [31:0] ra,
  output [31:0] sp,
  output [31:0] t0,
  output [31:0] t1,
  output [31:0] t2,
  output [31:0] s0,
  output [31:0] s1,
  output [31:0] a0
);

  wire ASel, BrEq, BrLT, BrUn, BSel, lb, lbu, lh, lhu, lui, lw, MemRW, PCSel, RegWEn;
  wire [1:0] WBSel;
  wire [2:0] funct3, ImmSel;
  wire [3:0] ALUSel;
  wire [4:0] rd, rs1, rs2;
  wire [6:0] funct7, opcode;
  wire [31:0] adder_1_out, alu_1_result, generateimm_1_imm, INS, load_extend_1_extended, main_1_read_data_1,
       main_1_read_data_2, main_2_readdata, multiplexer_1_out, multiplexer_2_out, multiplexer_3_out,
       multiplexer_4_out, multiplexer_5_out, multiplexer_6_out, PC, PC_4, PC_q;

  Multiplexer #(.width(32), .enable("false")) multiplexer_1 (
    .in0(INSTRUCTION), .in1(32'h13), .out(multiplexer_1_out), .sel(PCSel));
  regfile_main main_1 (
    .Read_Register_1_rs1(rs1), .Read_Register_2_rs2(rs2), .Write_Register_rd(rd),
    .Write_Data(multiplexer_6_out), .Write_Enable(RegWEn), .Clock(CLOCK), .Read_Data_1(main_1_read_data_1),
    .Read_Data_2(main_1_read_data_2), .ra(ra), .sp(sp), .t0(t0), .t1(t1), .t2(t2), .s0(s0), .s1(s1), .a0(a0));
  Register #(.width(32)) register_1 (.D(multiplexer_1_out), .en(1'b1), .clk(CLOCK), .Q(INS));  // open: clr
  BranchCom branchcom_1 (.DataA(main_1_read_data_1), .DataB(main_1_read_data_2), .BrUn(BrUn), .BrEq(BrEq), .BrLT(BrLT));
  Multiplexer #(.width(32), .enable("false")) multiplexer_2 (
    .in0(main_1_read_data_1), .in1(PC), .out(multiplexer_2_out), .sel(ASel));
  Multiplexer #(.width(32), .enable("false")) multiplexer_3 (
    .in0(main_1_read_data_2), .in1(generateimm_1_imm), .out(multiplexer_3_out), .sel(BSel));
  GenerateImm generateimm_1 (.Imm(generateimm_1_imm), .ImmSel(ImmSel), .Instruction(INS));
  split_instruction split_instruction_1 (
    .opcode(opcode), .funct3(funct3), .rs1(rs1), .OriginalInstruction(INS), .rs2(rs2), .rd(rd),
    .funct7(funct7));
  Multiplexer #(.width(32), .enable("false")) multiplexer_4 (
    .in0(multiplexer_2_out), .in1({32{1'b0}}), .out(multiplexer_4_out), .sel(lui));
  Adder #(.width(32)) adder_1 (.a(PC_q), .b(32'h4), .out(adder_1_out));  // open: cin, cout
  alu alu_1 (.A(multiplexer_4_out), .B(multiplexer_3_out), .ALUSel(ALUSel), .Result(alu_1_result));
  mem_main main_2 (
    .WriteAddr(alu_1_result), .WriteData(main_1_read_data_2), .MemRW(MemRW), .ReadData(main_2_readdata),
    .clk(CLOCK));
  Multiplexer #(.width(32), .enable("false")) multiplexer_5 (
    .in0(adder_1_out), .in1(alu_1_result), .out(multiplexer_5_out), .sel(PCSel));
  Register #(.width(32)) u_PC (.D(multiplexer_5_out), .en(1'b1), .clk(CLOCK), .Q(PC_q));  // open: clr
  Load_extend load_extend_1 (
    .lhu(lhu), .lw(lw), .origin(main_2_readdata), .lh(lh), .lbu(lbu), .extended(load_extend_1_extended));
  control control_1 (
    .lbu(lbu), .BSel(BSel), .lw(lw), .ASel(ASel), .lh(lh), .RegWEn(RegWEn), .lb(lb), .BrUn(BrUn),
    .ImmSel(ImmSel), .ALUSel(ALUSel), .BrLT(BrLT), .BrEq(BrEq), .opcode(opcode), .funct3(funct3),
    .funct7(funct7), .WBSel(WBSel), .lhu(lhu), .PCSel(PCSel), .lui(lui), .MemRW(MemRW));
  Register #(.width(32)) register_2 (.D(PC_q), .en(1'b1), .clk(CLOCK), .Q(PC));  // open: clr
  Shifter #(.width(32), .shift("lr")) shifter_1 (.in(PC_q), .\dist (5'b00010), .out(FETCH_ADDRESS));
  Multiplexer #(.select(2), .width(32), .enable("false")) multiplexer_6 (
    .in0(load_extend_1_extended), .in1(alu_1_result), .in2(PC_4), .out(multiplexer_6_out), .sel(WBSel));  // open: in3
  Adder #(.width(32)) adder_2 (.a(PC), .b(32'h4), .out(PC_4));  // open: cin, cout

  // Other names for the same wires on the sheet: clk = CLOCK; fetch_addr[31:0] = FETCH_ADDRESS

  // Notes on the sheet:
  //   Output
  //   Inputs/Outputs from run.circ. DO NOT MOVE THESE.
  //   Inputs
  //   Inputs/Outputs from run.circ. DO NOT MOVE THESE.
endmodule

module BranchCom (
  input  [31:0] DataA,
  input  [31:0] DataB,
  input  BrUn,
  output BrEq,
  output BrLT
);

  wire comparator_1_eq, comparator_1_lt, comparator_2_eq, comparator_2_lt;

  Comparator #(.width(32)) comparator_1 (.a(DataA), .b(DataB), .eq(comparator_1_eq), .lt(comparator_1_lt));  // open: gt
  Comparator #(.width(32), .mode("unsigned")) comparator_2 (
    .a(DataA), .b(DataB), .eq(comparator_2_eq), .lt(comparator_2_lt));  // open: gt
  Multiplexer #(.enable("false")) multiplexer_1 (.in0(comparator_1_eq), .in1(comparator_2_eq), .out(BrEq), .sel(BrUn));
  Multiplexer #(.enable("false")) multiplexer_2 (.in0(comparator_1_lt), .in1(comparator_2_lt), .out(BrLT), .sel(BrUn));

  // Other names for the same wires on the sheet: rs1[31:0] = DataA; rs2[31:0] = DataB
endmodule

module split_instruction (
  input  [31:0] OriginalInstruction,
  output [6:0] opcode,
  output [4:0] rd,
  output [2:0] funct3,
  output [4:0] rs1,
  output [4:0] rs2,
  output [6:0] funct7
);


  assign funct3 = OriginalInstruction[14:12];
  assign funct7 = OriginalInstruction[31:25];
  assign opcode = OriginalInstruction[6:0];
  assign rd = OriginalInstruction[11:7];
  assign rs1 = OriginalInstruction[19:15];
  assign rs2 = OriginalInstruction[24:20];
endmodule

module control (
  input  [6:0] funct7,
  input  [2:0] funct3,
  input  [6:0] opcode,
  input  BrEq,
  input  BrLT,
  output [3:0] ALUSel,
  output [2:0] ImmSel,
  output BrUn,
  output lb,
  output RegWEn,
  output lh,
  output ASel,
  output lw,
  output BSel,
  output lbu,
  output [1:0] WBSel,
  output lhu,
  output PCSel,
  output lui,
  output MemRW
);

  wire add0, addi0, and0, and_1_out, and_2_out, and_3_out, and_4_out, and_5_out, andi0, auipc0, beq0, bgeu0,
       blt0, bltu0, bne0, comparator_10_eq, comparator_11_eq, comparator_12_eq, comparator_13_eq,
       comparator_14_eq, comparator_15_eq, comparator_16_eq, comparator_17_eq, comparator_18_eq,
       comparator_19_eq, comparator_20_eq, comparator_21_eq, comparator_22_eq, comparator_23_eq,
       comparator_24_eq, comparator_25_eq, comparator_26_eq, comparator_27_eq, comparator_28_eq,
       comparator_29_eq, comparator_30_eq, comparator_31_eq, comparator_32_eq, comparator_33_eq,
       comparator_34_eq, comparator_35_eq, comparator_36_eq, comparator_37_eq, comparator_38_eq,
       comparator_39_eq, comparator_40_eq, comparator_41_eq, comparator_42_eq, comparator_43_eq,
       comparator_44_eq, comparator_45_eq, comparator_46_eq, comparator_47_eq, comparator_48_eq,
       comparator_49_eq, comparator_50_eq, comparator_51_eq, comparator_52_eq, comparator_53_eq,
       comparator_54_eq, div0, divu0, I_type_instruction, jal0, jalr0, Load_instruction, mul0, mulh0, mulhu0,
       not_1_out, not_2_out, or0, or_2_out, or_3_out, or_4_out, or_7_out, or_8_out, or_9_out, or_10_out,
       or_11_out, or_12_out, or_13_out, or_14_out, ori0, R_type_instruction, remu0, SB_type_instruction,
       sll0, slli0, slti0, srl0, srli0, sub0, xor0, xori0;
  wire [1:0] multiplexer_1_out, multiplexer_2_out;
  wire [2:0] multiplexer_17_out, multiplexer_18_out, multiplexer_19_out, multiplexer_20_out;
  wire [3:0] multiplexer_4_out, multiplexer_5_out, multiplexer_6_out, multiplexer_7_out, multiplexer_8_out,
       multiplexer_9_out, multiplexer_10_out, multiplexer_11_out, multiplexer_12_out, multiplexer_13_out,
       multiplexer_14_out, multiplexer_15_out;

  not not_1 (not_1_out, BrEq);
  not not_2 (not_2_out, BrLT);
  Comparator #(.width(7)) comparator_1 (.a(opcode), .b(7'b0110011), .eq(R_type_instruction));  // open: gt, lt
  Comparator #(.width(7)) comparator_2 (.a(opcode), .b(7'b0000011), .eq(Load_instruction));  // open: gt, lt
  Comparator #(.width(7)) comparator_3 (.a(opcode), .b(7'b0010011), .eq(I_type_instruction));  // open: gt, lt
  Comparator #(.width(7)) comparator_4 (.a(opcode), .b(7'b0100011), .eq(MemRW));  // open: gt, lt
  Comparator #(.width(7)) comparator_5 (.a(opcode), .b(7'b1100011), .eq(SB_type_instruction));  // open: gt, lt
  Comparator #(.width(7)) comparator_6 (.a(opcode), .b(7'b0010111), .eq(auipc0));  // open: gt, lt
  Comparator #(.width(7)) comparator_7 (.a(opcode), .b(7'b0110111), .eq(lui));  // open: gt, lt
  Comparator #(.width(7)) comparator_8 (.a(opcode), .b(7'b1101111), .eq(jal0));  // open: gt, lt
  Comparator #(.width(7)) comparator_9 (.a(opcode), .b(7'b1100111), .eq(jalr0));  // open: gt, lt
  and and_1 (and_1_out, beq0, BrEq);
  and and_2 (and_2_out, blt0, BrLT);
  and and_3 (and_3_out, bltu0, BrLT);
  and and_4 (and_4_out, bne0, not_1_out);
  and and_5 (and_5_out, bgeu0, not_2_out);
  Multiplexer #(.width(2), .enable("false")) multiplexer_1 (
    .in0(2'b00), .in1(2'b00), .out(multiplexer_1_out), .sel(Load_instruction));
  or or_1 (BrUn, bltu0, bgeu0);
  or or_2 (or_2_out, SB_type_instruction, MemRW);
  not not_3 (BSel, R_type_instruction);
  or or_3 (or_3_out, and_1_out, and_2_out, and_3_out, and_4_out, and_5_out);
  Multiplexer #(.width(2), .enable("false")) multiplexer_2 (
    .in0(multiplexer_1_out), .in1(2'b01), .out(multiplexer_2_out), .sel(or_4_out));
  or or_4 (or_4_out, I_type_instruction, R_type_instruction, lui, auipc0);
  not not_4 (RegWEn, or_2_out);
  or or_5 (ASel, SB_type_instruction, jal0, auipc0);
  or or_6 (PCSel, or_3_out, jal0, jalr0);
  Multiplexer #(.width(2), .enable("false")) multiplexer_3 (
    .in0(multiplexer_2_out), .in1(2'b10), .out(WBSel), .sel(or_7_out));
  or or_7 (or_7_out, jalr0, jal0);
  Multiplexer #(.width(4), .enable("false")) multiplexer_4 (
    .in0(4'b0000), .in1(4'b0001), .out(multiplexer_4_out), .sel(mul0));
  Multiplexer #(.width(4), .enable("false")) multiplexer_5 (
    .in0(multiplexer_4_out), .in1(4'b0010), .out(multiplexer_5_out), .sel(sub0));
  Comparator #(.width(3)) comparator_10 (.a(funct3), .b(3'b000), .eq(comparator_10_eq));  // open: gt, lt
  Comparator #(.width(7)) comparator_11 (.a(funct7), .b({7{1'b0}}), .eq(comparator_11_eq));  // open: gt, lt
  Comparator #(.width(3)) comparator_12 (.a(funct3), .b(3'b000), .eq(comparator_12_eq));  // open: gt, lt
  Comparator #(.width(7)) comparator_13 (.a(funct7), .b(7'b0000001), .eq(comparator_13_eq));  // open: gt, lt
  Comparator #(.width(3)) comparator_14 (.a(funct3), .b(3'b000), .eq(comparator_14_eq));  // open: gt, lt
  Comparator #(.width(7)) comparator_15 (.a(funct7), .b(7'b0100000), .eq(comparator_15_eq));  // open: gt, lt
  Comparator #(.width(3)) comparator_16 (.a(funct3), .b(3'b111), .eq(comparator_16_eq));  // open: gt, lt
  Comparator #(.width(7)) comparator_17 (.a(funct7), .b({7{1'b0}}), .eq(comparator_17_eq));  // open: gt, lt
  Comparator #(.width(3)) comparator_18 (.a(funct3), .b(3'b100), .eq(comparator_18_eq));  // open: gt, lt
  Comparator #(.width(3)) comparator_19 (.a(funct3), .b(3'b010), .eq(comparator_19_eq));  // open: gt, lt
  Comparator #(.width(3)) comparator_20 (.a(funct3), .b(3'b111), .eq(comparator_20_eq));  // open: gt, lt
  Comparator #(.width(3)) comparator_21 (.a(funct3), .b(3'b001), .eq(comparator_21_eq));  // open: gt, lt
  Multiplexer #(.width(4), .enable("false")) multiplexer_6 (
    .in0(multiplexer_5_out), .in1(4'b0011), .out(multiplexer_6_out), .sel(or_8_out));
  or or_8 (or_8_out, sll0, slli0);
  and and_6 (add0, comparator_10_eq, comparator_11_eq, R_type_instruction);
  and and_7 (mul0, comparator_12_eq, comparator_13_eq, R_type_instruction);
  and and_8 (sub0, comparator_14_eq, comparator_15_eq, R_type_instruction);
  and and_9 (and0, comparator_16_eq, comparator_17_eq, R_type_instruction);
  and and_10 (lbu, comparator_18_eq, Load_instruction);
  and and_11 (slti0, comparator_19_eq, I_type_instruction);
  and and_12 (andi0, comparator_20_eq, I_type_instruction);
  and and_13 (bne0, comparator_21_eq, SB_type_instruction);
  Multiplexer #(.width(4), .enable("false")) multiplexer_7 (
    .in0(multiplexer_6_out), .in1(4'b0100), .out(multiplexer_7_out), .sel(mulh0));
  Multiplexer #(.width(4), .enable("false")) multiplexer_8 (
    .in0(multiplexer_7_out), .in1(4'b0101), .out(multiplexer_8_out), .sel(mulhu0));
  Multiplexer #(.width(4), .enable("false")) multiplexer_9 (
    .in0(multiplexer_8_out), .in1(4'b0110), .out(multiplexer_9_out), .sel(or_9_out));
  or or_9 (or_9_out, xor0, xori0);
  Multiplexer #(.width(4), .enable("false")) multiplexer_10 (
    .in0(multiplexer_9_out), .in1(4'b0111), .out(multiplexer_10_out), .sel(div0));
  Comparator #(.width(3)) comparator_22 (.a(funct3), .b(3'b001), .eq(comparator_22_eq));  // open: gt, lt
  Comparator #(.width(7)) comparator_23 (.a(funct7), .b({7{1'b0}}), .eq(comparator_23_eq));  // open: gt, lt
  Comparator #(.width(3)) comparator_24 (.a(funct3), .b(3'b001), .eq(comparator_24_eq));  // open: gt, lt
  Comparator #(.width(7)) comparator_25 (.a(funct7), .b(7'b0000001), .eq(comparator_25_eq));  // open: gt, lt
  Comparator #(.width(3)) comparator_26 (.a(funct3), .b(3'b011), .eq(comparator_26_eq));  // open: gt, lt
  Comparator #(.width(7)) comparator_27 (.a(funct7), .b(7'b0000001), .eq(comparator_27_eq));  // open: gt, lt
  Comparator #(.width(3)) comparator_28 (.a(funct3), .b(3'b000), .eq(comparator_28_eq));  // open: gt, lt
  Comparator #(.width(3)) comparator_29 (.a(funct3), .b(3'b101), .eq(comparator_29_eq));  // open: gt, lt
  Comparator #(.width(3)) comparator_30 (.a(funct3), .b(3'b100), .eq(comparator_30_eq));  // open: gt, lt
  Comparator #(.width(3)) comparator_31 (.a(funct3), .b(3'b000), .eq(comparator_31_eq));  // open: gt, lt
  Comparator #(.width(3)) comparator_32 (.a(funct3), .b(3'b111), .eq(comparator_32_eq));  // open: gt, lt
  Multiplexer #(.width(4), .enable("false")) multiplexer_11 (
    .in0(multiplexer_10_out), .in1(4'b1000), .out(multiplexer_11_out), .sel(divu0));
  or or_10 (or_10_out, srl0, srli0);
  Multiplexer #(.width(4), .enable("false")) multiplexer_12 (
    .in0(multiplexer_11_out), .in1(4'b1001), .out(multiplexer_12_out), .sel(or_10_out));
  Multiplexer #(.width(4), .enable("false")) multiplexer_13 (
    .in0(multiplexer_12_out), .in1(4'b1010), .out(multiplexer_13_out), .sel(or_11_out));
  or or_11 (or_11_out, or0, ori0);
  and and_14 (sll0, comparator_22_eq, comparator_23_eq, R_type_instruction);
  and and_15 (mulh0, comparator_24_eq, comparator_25_eq, R_type_instruction);
  and and_16 (mulhu0, comparator_26_eq, comparator_27_eq, R_type_instruction);
  and and_17 (lb, comparator_28_eq, Load_instruction);
  and and_18 (lhu, comparator_29_eq, Load_instruction);
  and and_19 (xori0, comparator_30_eq, I_type_instruction);
  and and_20 (beq0, comparator_31_eq, SB_type_instruction);
  and and_21 (bgeu0, comparator_32_eq, SB_type_instruction);
  Multiplexer #(.width(4), .enable("false")) multiplexer_14 (
    .in0(multiplexer_13_out), .in1(4'b1011), .out(multiplexer_14_out), .sel(remu0));
  Multiplexer #(.width(4), .enable("false")) multiplexer_15 (
    .in0(multiplexer_14_out), .in1(4'b1100), .out(multiplexer_15_out), .sel(or_12_out));
  or or_12 (or_12_out, and0, andi0);
  Multiplexer #(.width(4), .enable("false")) multiplexer_16 (
    .in0(multiplexer_15_out), .in1(4'b1101), .out(ALUSel), .sel(slti0));
  Comparator #(.width(3)) comparator_33 (.a(funct3), .b(3'b100), .eq(comparator_33_eq));  // open: gt, lt
  Comparator #(.width(7)) comparator_34 (.a(funct7), .b({7{1'b0}}), .eq(comparator_34_eq));  // open: gt, lt
  Comparator #(.width(3)) comparator_35 (.a(funct3), .b(3'b100), .eq(comparator_35_eq));  // open: gt, lt
  Comparator #(.width(7)) comparator_36 (.a(funct7), .b(7'b0010000), .eq(comparator_36_eq));  // open: gt, lt
  Comparator #(.width(3)) comparator_37 (.a(funct3), .b(3'b101), .eq(comparator_37_eq));  // open: gt, lt
  Comparator #(.width(7)) comparator_38 (.a(funct7), .b(7'b0000001), .eq(comparator_38_eq));  // open: gt, lt
  Comparator #(.width(3)) comparator_39 (.a(funct3), .b(3'b001), .eq(comparator_39_eq));  // open: gt, lt
  Comparator #(.width(3)) comparator_40 (.a(funct3), .b(3'b000), .eq(comparator_40_eq));  // open: gt, lt
  Comparator #(.width(3)) comparator_41 (.a(funct3), .b(3'b101), .eq(comparator_41_eq));  // open: gt, lt
  Comparator #(.width(7)) comparator_42 (.a(funct7), .b({7{1'b0}}), .eq(comparator_42_eq));  // open: gt, lt
  Comparator #(.width(3)) comparator_43 (.a(funct3), .b(3'b100), .eq(comparator_43_eq));  // open: gt, lt
  and and_22 (xor0, comparator_33_eq, comparator_34_eq, R_type_instruction);
  and and_23 (div0, comparator_35_eq, comparator_36_eq, R_type_instruction);
  and and_24 (divu0, comparator_37_eq, comparator_38_eq, R_type_instruction);
  and and_25 (lh, comparator_39_eq, Load_instruction);
  and and_26 (addi0, comparator_40_eq, I_type_instruction);
  and and_27 (srli0, comparator_41_eq, comparator_42_eq, I_type_instruction);
  and and_28 (blt0, comparator_43_eq, SB_type_instruction);
  Multiplexer #(.width(3), .enable("false")) multiplexer_17 (
    .in0(3'b000), .in1(3'b000), .out(multiplexer_17_out), .sel(or_13_out));
  or or_13 (or_13_out, jalr0, Load_instruction, I_type_instruction);
  Multiplexer #(.width(3), .enable("false")) multiplexer_18 (
    .in0(multiplexer_17_out), .in1(3'b001), .out(multiplexer_18_out), .sel(MemRW));
  Multiplexer #(.width(3), .enable("false")) multiplexer_19 (
    .in0(multiplexer_18_out), .in1(3'b010), .out(multiplexer_19_out), .sel(SB_type_instruction));
  Comparator #(.width(3)) comparator_44 (.a(funct3), .b(3'b101), .eq(comparator_44_eq));  // open: gt, lt
  Comparator #(.width(7)) comparator_45 (.a(funct7), .b({7{1'b0}}), .eq(comparator_45_eq));  // open: gt, lt
  Comparator #(.width(3)) comparator_46 (.a(funct3), .b(3'b110), .eq(comparator_46_eq));  // open: gt, lt
  Comparator #(.width(7)) comparator_47 (.a(funct7), .b({7{1'b0}}), .eq(comparator_47_eq));  // open: gt, lt
  Comparator #(.width(3)) comparator_48 (.a(funct3), .b(3'b111), .eq(comparator_48_eq));  // open: gt, lt
  Comparator #(.width(7)) comparator_49 (.a(funct7), .b(7'b0000001), .eq(comparator_49_eq));  // open: gt, lt
  Comparator #(.width(3)) comparator_50 (.a(funct3), .b(3'b010), .eq(comparator_50_eq));  // open: gt, lt
  Comparator #(.width(3)) comparator_51 (.a(funct3), .b(3'b001), .eq(comparator_51_eq));  // open: gt, lt
  Comparator #(.width(7)) comparator_52 (.a(funct7), .b({7{1'b0}}), .eq(comparator_52_eq));  // open: gt, lt
  Comparator #(.width(3)) comparator_53 (.a(funct3), .b(3'b110), .eq(comparator_53_eq));  // open: gt, lt
  Comparator #(.width(3)) comparator_54 (.a(funct3), .b(3'b110), .eq(comparator_54_eq));  // open: gt, lt
  Multiplexer #(.width(3), .enable("false")) multiplexer_20 (
    .in0(multiplexer_19_out), .in1(3'b011), .out(multiplexer_20_out), .sel(or_14_out));
  or or_14 (or_14_out, lui, auipc0);
  and and_29 (srl0, comparator_44_eq, comparator_45_eq, R_type_instruction);
  and and_30 (or0, comparator_46_eq, comparator_47_eq, R_type_instruction);
  and and_31 (remu0, comparator_48_eq, comparator_49_eq, R_type_instruction);
  and and_32 (lw, comparator_50_eq, Load_instruction);
  and and_33 (slli0, comparator_51_eq, comparator_52_eq, I_type_instruction);
  and and_34 (ori0, comparator_53_eq, I_type_instruction);
  and and_35 (bltu0, comparator_54_eq, SB_type_instruction);
  Multiplexer #(.width(3), .enable("false")) multiplexer_21 (
    .in0(multiplexer_20_out), .in1(3'b100), .out(ImmSel), .sel(jal0));

  // Other names for the same wires on the sheet: lb0 = lb; lbu0 = lbu; lh0 = lh; lhu0 = lhu; lui0 = lui; lw0 = lw;
  //   sw0 = MemRW

  // Notes on the sheet:
  //   0 - add/addi/lui/auipc/branch/jal/jalr
endmodule

module GenerateImm (
  input  [31:0] Instruction,
  input  [2:0] ImmSel,
  output [31:0] Imm
);

  wire comparator_1_eq, comparator_2_eq, comparator_3_eq, comparator_4_eq;
  wire [31:0] bit_extender_1_out, bit_extender_2_out, bit_extender_3_out, bit_extender_4_out,
       multiplexer_1_out, multiplexer_2_out, multiplexer_3_out;

  assign bit_extender_1_out = {{20{Instruction[31]}}, Instruction[31:20]};  // Bit_Extender bit_extender_1
  assign bit_extender_2_out = {{20{Instruction[31]}}, {Instruction[31:25], Instruction[11:7]}};  // Bit_Extender bit_extender_2
  Comparator #(.width(3)) comparator_1 (.a(ImmSel), .b(3'b001), .eq(comparator_1_eq));  // open: gt, lt
  assign bit_extender_3_out = {{19{Instruction[31]}}, {Instruction[31], Instruction[7], Instruction[30:25], Instruction[11:8], 1'b0}};  // Bit_Extender bit_extender_3
  Comparator #(.width(3)) comparator_2 (.a(ImmSel), .b(3'b010), .eq(comparator_2_eq));  // open: gt, lt
  Multiplexer #(.width(32), .enable("false")) multiplexer_1 (
    .in0(bit_extender_1_out), .in1(bit_extender_2_out), .out(multiplexer_1_out), .sel(comparator_1_eq));
  Multiplexer #(.width(32), .enable("false")) multiplexer_2 (
    .in0(multiplexer_1_out), .in1(bit_extender_3_out), .out(multiplexer_2_out), .sel(comparator_2_eq));
  Comparator #(.width(3)) comparator_3 (.a(ImmSel), .b(3'b011), .eq(comparator_3_eq));  // open: gt, lt
  Multiplexer #(.width(32), .enable("false")) multiplexer_3 (
    .in0(multiplexer_2_out), .in1({Instruction[31:12], {12{1'b0}}}), .out(multiplexer_3_out),
    .sel(comparator_3_eq));
  assign bit_extender_4_out = {{19{Instruction[31]}}, {Instruction[31], Instruction[20], Instruction[30:21], 1'b0}};  // Bit_Extender bit_extender_4
  Comparator #(.width(3)) comparator_4 (.a(ImmSel), .b(3'b100), .eq(comparator_4_eq));  // open: gt, lt
  Multiplexer #(.width(32), .enable("false")) multiplexer_4 (
    .in0(multiplexer_3_out), .in1(bit_extender_4_out), .out(Imm), .sel(comparator_4_eq));

  // Other names for the same wires on the sheet: inst_imm[31:0] = Instruction
endmodule

module Load_extend (
  input  [31:0] origin,
  input  lh,
  input  lw,
  input  lbu,
  input  lhu,
  output [31:0] extended
);

  wire [31:0] bit_extender_1_out, bit_extender_2_out, bit_extender_3_out, bit_extender_4_out,
       multiplexer_1_out, multiplexer_2_out, multiplexer_3_out;

  assign bit_extender_1_out = {{24{origin[7]}}, origin[7:0]};  // Bit_Extender bit_extender_1
  assign bit_extender_2_out = {{16{origin[15]}}, origin[15:0]};  // Bit_Extender bit_extender_2
  assign bit_extender_3_out = {{24{1'b0}}, origin[7:0]};  // Bit_Extender bit_extender_3
  assign bit_extender_4_out = {{16{1'b0}}, origin[15:0]};  // Bit_Extender bit_extender_4
  Multiplexer #(.width(32), .enable("false")) multiplexer_1 (
    .in0(bit_extender_1_out), .in1(bit_extender_2_out), .out(multiplexer_1_out), .sel(lh));
  Multiplexer #(.width(32), .enable("false")) multiplexer_2 (
    .in0(multiplexer_1_out), .in1(origin), .out(multiplexer_2_out), .sel(lw));
  Multiplexer #(.width(32), .enable("false")) multiplexer_3 (
    .in0(multiplexer_2_out), .in1(bit_extender_3_out), .out(multiplexer_3_out), .sel(lbu));
  Multiplexer #(.width(32), .enable("false")) multiplexer_4 (
    .in0(multiplexer_3_out), .in1(bit_extender_4_out), .out(extended), .sel(lhu));

  // Notes on the sheet:
  //   lb
endmodule
